# Fritzing sketch Door Controller RC522 (saved by Fritzing 0.9.3b)
circuit board: 9.70172cm x 6.63756cm
circuit board: 4.72472cm x 5.37351cm
circuit board: 8.10287cm x 5.53334cm
breadboards: 2

parts:
  Arduino_Uno = Arduino Uno (Rev3)
  LED1 = RGB LED - (4 legs) [package="5 mm [THT]"]
  R2 = Resistor [tolerance=±5% resistance=470k package=THT]
  RC522 = RFID-RC522-v2
  Raspberry_Pi1 = Raspberry Pi 2
  R3 = Resistor [tolerance=±5% resistance=6.8k package="1206 [SMD]"]
  R4 = Resistor [tolerance=±5% resistance=6.8k package="1206 [SMD]"]

nets:
  N1: Arduino_Uno.A4/SDA, Raspberry_Pi1.GPIO2, R3.Pin_0
  N2: Arduino_Uno.A5/SCL, Raspberry_Pi1.GPIO3, R4.Pin_0
  N3: Arduino_Uno.D9_PWM, RC522.RST
  N4: Arduino_Uno.D10_PWM/SS, RC522.SDA
  N5: Arduino_Uno.D11_PWM/MOSI, RC522.MOSI
  N6: Arduino_Uno.D12/MISO, RC522.MISO
  N7: Arduino_Uno.D13/SCK, RC522.SCK
  N8: Arduino_Uno.D5_PWM, LED1.blue_cathode
  N9: Arduino_Uno.D6_PWM, LED1.green_cathode
  N10: Arduino_Uno.D7, LED1.red_cathode
  3V3: Arduino_Uno.3V3, RC522.3.3V
  GND: Arduino_Uno.GND, R2.Pin_0, RC522.GND, Raspberry_Pi1.GND
  N11: LED1.common_anode, R2.Pin_1
  N12: Raspberry_Pi1.5V, R3.Pin_1, R4.Pin_1

custom parts:
  RFID-RC522-v2: A simple China made RFID-RC522 Reader; do check the pin labels, as this is a MFRC522 based clone.
